// Logisim project projecto3.circ as structural Verilog: 1 circuit, main circuit main
module main (
  input  [7:0] in_1,
  output [5:0] RESULTADO,
  output out_3,
  output [7:0] out_4
);

  wire button_1_out, clock_1_out;
  wire [5:0] adder_2_out, adder_3_out, multiplexer_1_out, multiplexer_2_out, multiplexer_3_out,
       multiplexer_4_out, not_1_out, subtractor_1_out;
  wire [7:0] adder_1_out, register_1_q;

  ROM rom_1 (.addr(register_1_q), .data({out_4[7:3], out_3, out_4[1:0]}));
  Button button_1 (.out(button_1_out));
  Clock clock_1 (.out(clock_1_out));
  Adder adder_1 (.a(in_1), .b(register_1_q), .out(adder_1_out), .cin(1'b1));  // open: cout
  Register register_1 (.D(adder_1_out), .clk(clock_1_out), .Q(register_1_q), .clr(button_1_out));  // open: en
  assign not_1_out = ~RESULTADO;  // NOT_Gate not_1, 6 bits wide
  Adder #(.width(6)) adder_2 (.a(RESULTADO), .b({out_4[7:3], out_3}), .out(adder_2_out));  // open: cin, cout
  Subtractor #(.width(6)) subtractor_1 (
    .a(RESULTADO), .b({out_4[7:3], out_3}), .out(subtractor_1_out));  // open: bin, bout
  Multiplexer #(.width(6)) multiplexer_1 (
    .in0(RESULTADO), .in1({6{1'b0}}), .out(multiplexer_1_out), .sel(RESULTADO[5]));
  Adder #(.width(6)) adder_3 (.a(not_1_out), .b(6'b000001), .out(adder_3_out));  // open: cin, cout
  Multiplexer #(.width(6)) multiplexer_2 (
    .in0(RESULTADO), .in1(adder_3_out), .out(multiplexer_2_out), .sel(RESULTADO[5]));
  Multiplexer #(.select(2), .width(6)) multiplexer_3 (
    .in0({out_4[7:3], out_3}), .in1(adder_2_out), .in2(subtractor_1_out), .in3(multiplexer_4_out),
    .out(multiplexer_3_out), .sel(out_4[1:0]));
  Multiplexer #(.width(6)) multiplexer_4 (
    .in0(multiplexer_1_out), .in1(multiplexer_2_out), .out(multiplexer_4_out), .sel(out_3));
  Register #(.width(6)) register_2 (
    .D(multiplexer_3_out), .clk(clock_1_out), .Q(RESULTADO), .clr(button_1_out));  // open: en

  assign out_4[2] = out_3;

  // Notes on the sheet:
  //   contents of rom_1 (hex, n*v repeats v):
  //   28 7 d8 7 0 0 28 3 d8 3 0 0 d8 2f
  //   MUX Relu
  //   MUX Abs
  //   MUX principal
  //   MUX relu/abs
endmodule
